# Fritzing sketch Sketch (saved by Fritzing 0.9.3b)

parts:
  Bauteil1 = Arduino Mega 2560 (Rev3)
  GY1 = MPU-6050 Board GY-521 [form="♀ (female)" package=THT]
  U1 = ESP8266 WiFi Module [part_number=ESP8266]
  FrontRight_ESC = Basic Servo
  RearLeft_ESC = Basic Servo
  FrontLeft_ESC = Basic Servo
  RearRight_ESC = Basic Servo

nets:
  N1: Bauteil1.D21/SCL, GY1.pin3
  N2: Bauteil1.D20/SDA, GY1.pin4
  N3: Bauteil1.D19/RX1, U1.TXD
  N4: Bauteil1.D18/TX1, U1.RXD
  N5: Bauteil1.D12_PWM, FrontLeft_ESC.gnd
  N6: Bauteil1.D11_PWM, RearRight_ESC.gnd
  N7: Bauteil1.D10_PWM, RearLeft_ESC.gnd
  N8: Bauteil1.D9_PWM, FrontRight_ESC.gnd
  N9: Bauteil1.5V, GY1.pin1
  GND: Bauteil1.GND, U1.GND

custom parts:
  MPU-6050 Board GY-521: Acelerometro y Giroscopio MPU-6050 Board GY-521
  ESP8266 WiFi Module: Generic WiFi Module based on the ESP8266 with onboard PCB antenna and UART communications
